// Logisim project Phase1_Day1_Comparators.circ as structural Verilog: 4 circuits, main circuit universal_4bit_comparator
module universal_4bit_comparator (
  input  eq,
  input  mo,
  input  gl,
  input  [3:0] inA,
  input  [3:0] inB,
  output E,
  output L,
  output G
);

  wire magitude_1bit_comparator_1_aeb, magitude_1bit_comparator_1_agb, magitude_1bit_comparator_1_alb,
       magitude_1bit_comparator_2_aeb, magitude_1bit_comparator_2_agb, magitude_1bit_comparator_2_alb,
       msb_sing_comparator_1_aeb, msb_sing_comparator_1_agb, msb_sing_comparator_1_alb;

  msb_sing_comparator msb_sing_comparator_1 (
    .equal(eq), .less(gl), .great(gl), .A(inA[3]), .mode(mo), .B(inB[3]), .aEb(msb_sing_comparator_1_aeb),
    .aLb(msb_sing_comparator_1_alb), .aGb(msb_sing_comparator_1_agb));
  magitude_1bit_comparator magitude_1bit_comparator_1 (
    .equal(msb_sing_comparator_1_aeb), .less(msb_sing_comparator_1_alb), .great(msb_sing_comparator_1_agb),
    .A(inA[2]), .B(inB[2]), .aEb(magitude_1bit_comparator_1_aeb), .aLb(magitude_1bit_comparator_1_alb),
    .aGb(magitude_1bit_comparator_1_agb));
  magitude_1bit_comparator magitude_1bit_comparator_2 (
    .equal(magitude_1bit_comparator_1_aeb), .less(magitude_1bit_comparator_1_alb),
    .great(magitude_1bit_comparator_1_agb), .A(inA[1]), .B(inB[1]), .aEb(magitude_1bit_comparator_2_aeb),
    .aLb(magitude_1bit_comparator_2_alb), .aGb(magitude_1bit_comparator_2_agb));
  magitude_1bit_comparator magitude_1bit_comparator_3 (
    .equal(magitude_1bit_comparator_2_aeb), .less(magitude_1bit_comparator_2_alb),
    .great(magitude_1bit_comparator_2_agb), .A(inA[0]), .B(inB[0]), .aEb(E), .aLb(L), .aGb(G));
endmodule

module magitude_1bit_comparator (
  input  equal,
  input  less,
  input  great,
  input  A,
  input  B,
  output aEb,
  output aLb,
  output aGb
);

  wire and_1_out, and_2_out, not_1_out, not_2_out, xnor_1_out;

  not not_1 (not_1_out, A);
  not not_2 (not_2_out, B);
  xnor xnor_1 (xnor_1_out, A, B);
  and and_1 (and_1_out, B, equal, not_1_out);
  and and_2 (and_2_out, A, equal, not_2_out);
  and and_3 (aEb, equal, xnor_1_out);
  or or_1 (aLb, and_1_out, less);
  or or_2 (aGb, great, and_2_out);
endmodule

module msb_sing_comparator (
  input  equal,
  input  less,
  input  great,
  input  A,
  input  mode,
  input  B,
  output aEb,
  output aLb,
  output aGb
);

  wire and_1_out, and_2_out, not_1_out, not_2_out, xnor_1_out, xor_1_out, xor_2_out;

  xor xor_1 (xor_1_out, A, mode);
  not not_1 (not_1_out, xor_1_out);
  xor xor_2 (xor_2_out, B, mode);
  not not_2 (not_2_out, xor_2_out);
  xnor xnor_1 (xnor_1_out, xor_1_out, xor_2_out);
  and and_1 (and_1_out, xor_2_out, equal, not_1_out);
  and and_2 (and_2_out, xor_1_out, equal, not_2_out);
  and and_3 (aEb, equal, xnor_1_out);
  or or_1 (aLb, and_1_out, less);
  or or_2 (aGb, great, and_2_out);
endmodule

module safe_zone_logic (
  input  in_1,
  input  in_2,
  input  in_3,
  input  [3:0] in_4,
  input  [3:0] in_5,
  input  [3:0] in_6
);

  wire nand_1_out, or_1_out, or_2_out, universal_4bit_comparator_1_e, universal_4bit_comparator_1_l,
       universal_4bit_comparator_2_e, universal_4bit_comparator_2_g;

  universal_4bit_comparator universal_4bit_comparator_1 (
    .eq(in_2), .mo(in_3), .gl(in_1), .inA(in_4), .inB(in_5), .E(universal_4bit_comparator_1_e),
    .L(universal_4bit_comparator_1_l));  // open: G
  universal_4bit_comparator universal_4bit_comparator_2 (
    .eq(in_2), .mo(in_3), .gl(in_1), .inA(in_4), .inB(in_6), .E(universal_4bit_comparator_2_e),
    .G(universal_4bit_comparator_2_g));  // open: L
  or or_1 (or_1_out, universal_4bit_comparator_1_e, universal_4bit_comparator_1_l);
  or or_2 (or_2_out, universal_4bit_comparator_2_e, universal_4bit_comparator_2_g);
  nand nand_1 (nand_1_out, or_1_out, or_2_out);
  LED led_1 (.in(nand_1_out));
endmodule
