// Logisim project Phase1_Day2_NAND_Logic.circ as structural Verilog: 1 circuit, main circuit nandlogic
module nandlogic (
  input  A,
  input  B,
  input  C,
  input  D,
  output Y
);

  wire nand_1_out, nand_2_out, nand_3_out, nand_4_out, nand_5_out, nand_6_out, nand_7_out, nand_8_out;

  nand nand_1 (nand_1_out, A, A);
  nand nand_2 (nand_2_out, B, B);
  nand nand_3 (nand_3_out, D, nand_2_out);
  nand nand_4 (nand_4_out, nand_1_out, B);
  nand nand_5 (nand_5_out, nand_4_out, nand_4_out);
  nand nand_6 (nand_6_out, nand_3_out, nand_3_out);
  nand nand_7 (nand_7_out, nand_5_out, D);
  nand nand_8 (nand_8_out, nand_6_out, C);
  nand nand_9 (Y, nand_7_out, nand_8_out);
endmodule
