// Logisim project BCD_to_Gray.circ as structural Verilog: 1 circuit, main circuit bin_to_gray
module bin_to_gray (
  input  a,
  input  b,
  input  c,
  input  d,
  output g3,
  output g2,
  output g1,
  output g0
);

  wire and_1_out, and_2_out, not_1_out;

  not not_1 (not_1_out, c);
  or or_1 (g2, a, b);
  and and_1 (and_1_out, b, not_1_out);
  and and_2 (and_2_out, c, a);
  xor xor_1 (g0, c, d);
  or or_2 (g1, and_1_out, and_2_out);

  assign g3 = a;
endmodule
