// Logisim project Dual_Output_Fib_Div3.circ as structural Verilog: 1 circuit, main circuit main
module main (
  input  A,
  input  B,
  input  C,
  input  D,
  output F1,
  output F2
);

  wire a_t, and_1_out, and_2_out, and_3_out, and_4_out, and_5_out, and_6_out, and_7_out, and_8_out,
       and_9_out, and_10_out, b_t, c_t, d_t;

  not not_1 (a_t, A);
  not not_2 (b_t, B);
  not not_3 (c_t, C);
  not not_4 (d_t, D);
  and and_1 (and_1_out, a_t, b_t, C);
  and and_2 (and_2_out, b_t, a_t, D);
  and and_3 (and_3_out, b_t, c_t, d_t, A);
  and and_4 (and_4_out, B, c_t, D);
  and and_5 (and_5_out, a_t, b_t, c_t, d_t);
  and and_6 (and_6_out, a_t, C, D, b_t);
  and and_7 (and_7_out, a_t, B, C, d_t);
  and and_8 (and_8_out, b_t, A, D, c_t);
  and and_9 (and_9_out, c_t, B, A, d_t);
  and and_10 (and_10_out, B, A, C, D);
  or or_1 (F1, and_1_out, and_2_out, and_3_out, and_4_out);
  or or_2 (F2, and_5_out, and_10_out, and_6_out, and_7_out, and_8_out, and_9_out);
endmodule
